// Logisim project ALU.circ as structural Verilog: 1 circuit, main circuit ALU
module ALU (
  input  [19:0] N0,
  input  [19:0] N1,
  input  [2:0] S3,
  input  ES,
  output O,
  output [19:0] R,
  output E
);

  wire multiplexer_1_out, n20_bit_adder_1_o, n20bitsubtractor_1_o, nor_1_out;
  wire [19:0] n20_bit_adder_1_s, n20bitbitwiseand_1_r, n20bitbitwiseor_1_s, n20bitbitwisexor_1_r,
       n20bitsubtractor_1_d;

  nor nor_1 (nor_1_out, S3[2], S3[1]);
  and and_1 (O, nor_1_out, multiplexer_1_out);
  Multiplexer #(.disabled(0), .enable("false")) multiplexer_1 (
    .in0(n20_bit_adder_1_o), .in1(n20bitsubtractor_1_o), .out(multiplexer_1_out), .sel(S3[0]));
  _20_Bit_Adder u_20_bit_adder_1 (.N0(N0), .N1(N1), .S(n20_bit_adder_1_s), .O(n20_bit_adder_1_o));
  _20BitSubtractor u_20bitsubtractor_1 (.N0(N0), .O(n20bitsubtractor_1_o), .D(n20bitsubtractor_1_d), .N1(N1));
  _20BitBitwiseAnd u_20bitbitwiseand_1 (.N0(N0), .N1(N1), .R(n20bitbitwiseand_1_r));
  _20BitBitwiseOr u_20bitbitwiseor_1 (.I0(N0), .I1(N1), .S(n20bitbitwiseor_1_s));
  _20BitBitwiseXor u_20bitbitwisexor_1 (.N0(N0), .N1(N1), .R(n20bitbitwisexor_1_r));
  EqualityChecker equalitychecker_1 (.N0(N0), .N1(N1), .S(ES), .R(E));
  Multiplexer #(.select(3), .width(20), .disabled(0), .enable("false")) multiplexer_2 (
    .in0(n20_bit_adder_1_s), .in1(n20bitsubtractor_1_d), .in2(n20bitbitwiseand_1_r),
    .in3(n20bitbitwiseor_1_s), .in4(n20bitbitwisexor_1_r), .out(R), .sel(S3));  // open: in5, in6, in7

  // Notes on the sheet:
  //   O: pull=down
  //   S3: pull=down
  //   N1: pull=down
  //   N0: pull=down
  //   E: pull=down
  //   ES: pull=down
  //   R: pull=down
endmodule
