// Logisim project FullAdder.circ as structural Verilog: 1 circuit, main circuit Full Adder
module Full_Adder (
  input  C_in,
  input  A,
  input  B,
  output S,
  output C_out
);

  wire half_adder_1_c, half_adder_1_s, half_adder_2_c;

  Half_Adder half_adder_1 (.A(A), .B(B), .S(half_adder_1_s), .C(half_adder_1_c));
  Half_Adder half_adder_2 (.A(C_in), .B(half_adder_1_s), .S(S), .C(half_adder_2_c));
  or or_1 (C_out, half_adder_2_c, half_adder_1_c);
endmodule
