// Logisim project CPU.circ as structural Verilog: 1 circuit, main circuit CPU
module CPU (
  input  Fetch,
  output [9:0] out_2
);

  wire clock_1_out, memory_1_p4;
  wire [9:0] n10bitincrementer_1_o;

  Clock clock_1 (.out(clock_1_out));
  // Memory memory_1: pin names not known; wires that end beside it: out_2, Fetch, clock_1_out, memory_1_p4
  _10BitRegister PC (.C(clock_1_out), .E(Fetch), .I(n10bitincrementer_1_o), .Q(out_2));
  _10BitIncrementer u_10bitincrementer_1 (.I(out_2), .O(n10bitincrementer_1_o));

  // Notes on the sheet:
  //   Fetch: pull=down
  //   out_2: pull=down
endmodule
