// Logisim project ControlUnit.circ as structural Verilog: 2 circuits, main circuit Control Unit
module Control_Unit (
  input  [19:0] I,
  input  C,
  output FO,
  output EX,
  output SR,
  output FE
);

  wire decoder_1_out1, n3bitregister_1_p2;
  wire [2:0] n3bitregister_1_p3, n3bitregister_1_p4;

  // _3BitRegister 3bitregister_1: pin names not known; wires that end beside it: C, n3bitregister_1_p2, n3bitregister_1_p3, n3bitregister_1_p4
  Decoder_part #(.select(3), .disabled(0), .enable("false")) decoder_1 (
    .out0(FE), .out1(decoder_1_out1), .out2(FO), .out3(EX), .out4(SR), .sel(n3bitregister_1_p4));  // open: out5, out6, out7
  Decoder decoder_2 (
    .E(decoder_1_out1), .in_2(I), .NEXT(n3bitregister_1_p3));  // open: IMM7, IMM10, ALUS, IMM, LD, ST, PUSH, POP, JUMP, BE, BES, DR, SR1, SR2

  // Notes on the sheet:
  //   EX: pull=down
  //   I: pull=down
  //   C: pull=down
  //   FE: pull=down
  //   FO: pull=down
  //   SR: pull=down
endmodule

module Decoder (
  input  E,
  input  [19:0] in_2,
  output [6:0] IMM7,
  output [9:0] IMM10,
  output [2:0] ALUS,
  output IMM,
  output LD,
  output ST,
  output PUSH,
  output POP,
  output JUMP,
  output BE,
  output BES,
  output [3:0] DR,
  output [3:0] SR1,
  output [3:0] SR2,
  output [2:0] NEXT
);

  wire decoder_1_out1, decoder_1_out2, decoder_1_out3, decoder_1_out4, decoder_1_out5, decoder_1_out6,
       decoder_1_out7, decoder_1_out8, decoder_1_out9, decoder_1_out10, decoder_1_out16, or_1_out, or_4_out,
       or_5_out, or_7_out;
  wire [1:0] or_10_out, or_12_out;

  or or_1 (or_1_out, decoder_1_out3, decoder_1_out4);
  or or_2 (ALUS[1], or_5_out, or_4_out);
  or or_3 (ALUS[0], or_1_out, or_4_out);
  or or_4 (or_4_out, decoder_1_out7, decoder_1_out8);
  or or_5 (or_5_out, decoder_1_out5, decoder_1_out6);
  or or_6 (ALUS[2], decoder_1_out9, decoder_1_out10);
  Decoder_part #(.select(5), .disabled(0)) decoder_1 (
    .out1(decoder_1_out1), .out2(decoder_1_out2), .out3(decoder_1_out3), .out4(decoder_1_out4),
    .out5(decoder_1_out5), .out6(decoder_1_out6), .out7(decoder_1_out7), .out8(decoder_1_out8),
    .out9(decoder_1_out9), .out10(decoder_1_out10), .out11(LD), .out12(ST), .out13(PUSH), .out14(POP),
    .out15(JUMP), .out16(decoder_1_out16), .out17(BES), .sel(in_2[19:15]), .en(E));  // open: out0, out18, out19, out20, out21, out22, out23, out24, out25, out26, out27, out28, out29, out30, out31
  Multiplexer #(.select(2), .width(4), .disabled(0), .enable("false")) multiplexer_1 (
    .in0(in_2[14:11]), .in1(in_2[13:10]), .in2(in_2[11:8]), .in3(in_2[3:0]), .out(DR), .sel(or_10_out));
  Multiplexer #(.select(3), .width(4), .disabled(0), .enable("false")) multiplexer_2 (
    .in0(in_2[14:11]), .in1(in_2[13:10]), .in2(in_2[10:7]), .in3(in_2[7:4]), .in4(in_2[3:0]), .out(SR1),
    .sel({PUSH, or_12_out}));  // open: in5, in6, in7
  Multiplexer #(.width(4), .enable("false")) multiplexer_3 (
    .in0(in_2[10:7]), .in1(in_2[3:0]), .out(SR2), .sel(or_7_out));
  or or_7 (or_7_out, decoder_1_out9, decoder_1_out7, decoder_1_out5, decoder_1_out3, decoder_1_out1);
  or or_8 (IMM, decoder_1_out2, decoder_1_out4, decoder_1_out6, decoder_1_out8, decoder_1_out10);
  or or_9 (BE, BES, decoder_1_out16);
  or or_10 (or_10_out[0], LD, POP);
  or or_11 (or_10_out[1], or_7_out, POP);
  or or_12 (or_12_out[0], or_7_out, ST);
  or or_13 (or_12_out[1], or_7_out, IMM);

  assign IMM7 = in_2[6:0];
  assign IMM10 = in_2[9:0];

  // Notes on the sheet:
  //   SR1: pull=down
  //   IMM10: pull=down
  //   ALUS: pull=down
  //   POP: pull=down
  //   PUSH: pull=down
  //   BE: pull=down
  //   IMM: pull=down
  //   in_2: pull=down
  //   DR: pull=down
  //   JUMP: pull=down
  //   IMM7: pull=down
  //   LD: pull=down
  //   SR2: pull=down
  //   ST: pull=down
  //   NEXT: pull=down
  //   BES: pull=down
endmodule
