// Logisim project Terminator.circ as structural Verilog: 1 circuit, main circuit Terminator
module Terminator (
  input  clk,
  input  t_0,
  input  Decode,
  input  Halt_Instruction,
  input  Stack_Overflow,
  input  Instruction_End,
  input  PC_Overflow,
  output Halted
);

  wire and_1_out, and_2_out, Delay_q, Halted_q, or_1_out, PCOverflowed_q, Started_q;

  RisingEdgeTriggeredDFlipFlop Started (.D(Decode), .clk(clk), .Q(Started_q), .W_Enable(Decode), .reset(t_0));
  RisingEdgeTriggeredDFlipFlop PCOverflowed (
    .D(PC_Overflow), .clk(clk), .Q(PCOverflowed_q), .W_Enable(PC_Overflow), .reset(t_0));
  and and_1 (and_1_out, Started_q, Halt_Instruction);
  and and_2 (and_2_out, Instruction_End, PCOverflowed_q);
  FallingEdgeTriggeredDFlipFlop Delay (.D(1'b1), .clk(and_2_out), .Q(Delay_q), .W_Enable(1'b1));
  or or_1 (or_1_out, and_1_out, Stack_Overflow, Delay_q);
  RisingEdgeTriggeredDFlipFlop u_Halted (.D(or_1_out), .clk(or_1_out), .Q(Halted_q), .W_Enable(or_1_out), .reset(t_0));
  or or_2 (Halted, Halted_q, or_1_out);

  // Notes on the sheet:
  //   t_0: pull=down
  //   PC_Overflow: pull=down
  //   Instruction_End: pull=down
  //   Decode: pull=down
  //   Halted: pull=down
  //   Stack_Overflow: pull=down
  //   clk: pull=down
  //   Halt_Instruction: pull=down
endmodule
