// Logisim project DLatch.circ as structural Verilog: 1 circuit, main circuit DLatch
module DLatch (
  input  D,
  input  C,
  output Q
);

  wire and_1_out, and_2_out, nor_1_out, not_1_out;

  not not_1 (not_1_out, D);
  and and_1 (and_1_out, D, C);
  and and_2 (and_2_out, C, not_1_out);
  nor nor_1 (nor_1_out, and_1_out, Q);
  nor nor_2 (Q, nor_1_out, and_2_out);

  // Notes on the sheet:
  //   Q: pull=down
  //   C: pull=down
  //   D: pull=down
endmodule
