// Logisim project FallingEdgeTriggeredDFlipFlop.circ as structural Verilog: 1 circuit, main circuit FallingEdgeTriggeredDFlipFlop
module FallingEdgeTriggeredDFlipFlop (
  input  D,
  input  E,
  input  C,
  output Q
);

  wire dlatch_1_q, multiplexer_1_out, not_1_out;

  Multiplexer #(.enable("false")) multiplexer_1 (.in0(Q), .in1(D), .out(multiplexer_1_out), .sel(E));
  DLatch dlatch_1 (.D(multiplexer_1_out), .C(C), .Q(dlatch_1_q));
  not not_1 (not_1_out, C);
  DLatch dlatch_2 (.D(dlatch_1_q), .C(not_1_out), .Q(Q));

  // Notes on the sheet:
  //   C: pull=down
  //   D: pull=down
  //   E: pull=down
  //   Q: pull=down
endmodule
