// Logisim project RisingEdgeTriggeredDFlipFlop.circ as structural Verilog: 1 circuit, main circuit RisingEdgeTriggeredDFlipFlop
module RisingEdgeTriggeredDFlipFlop (
  input  D,
  input  W_Enable,
  input  clk,
  output Q
);

  wire dlatch_1_q, multiplexer_1_out, not_1_out;

  Multiplexer #(.enable("false")) multiplexer_1 (.in0(Q), .in1(D), .out(multiplexer_1_out), .sel(W_Enable));
  not not_1 (not_1_out, clk);
  DLatch dlatch_1 (.D(multiplexer_1_out), .C(not_1_out), .Q(dlatch_1_q));
  DLatch dlatch_2 (.D(dlatch_1_q), .C(clk), .Q(Q));

  // Notes on the sheet:
  //   D: pull=down
  //   W_Enable: pull=down
  //   Q: pull=down
  //   clk: pull=down
endmodule
