// Logisim project Memory.circ as structural Verilog: 1 circuit, main circuit Memory
module Memory (
  input  [9:0] A,
  input  [19:0] D,
  input  C,
  input  MS,
  input  OS,
  output [19:0] D_2
);

  wire not_1_out, not_2_out, not_3_out;
  wire [19:0] ram_1_data, ram_2_data;

  not not_1 (not_1_out, OS);
  not not_2 (not_2_out, MS);
  RAM #(.addrWidth(10), .dataWidth(20), .bus("separate")) ram_1 (
    .addr(A), .din(D), .data(ram_1_data), .str(OS), .sel(not_2_out), .clk(C), .ld(not_3_out));  // open: clr
  not not_3 (not_3_out, OS);
  Multiplexer #(.width(20), .disabled(0)) multiplexer_1 (
    .in0(ram_1_data), .in1(ram_2_data), .out(D_2), .sel(MS), .en(not_1_out));
  RAM #(.addrWidth(10), .dataWidth(20), .bus("separate")) ram_2 (
    .addr(A), .din(D), .data(ram_2_data), .str(OS), .sel(MS), .clk(C), .ld(not_3_out));  // open: clr

  // Notes on the sheet:
  //   OS: pull=down
  //   A: pull=down
  //   D_2: pull=down
  //   D: pull=down
  //   C: pull=down
  //   MS: pull=down
  //   Data Memory
  //   Instruction Memory
endmodule
