// Logisim project 10BitRegister.circ as structural Verilog: 1 circuit, main circuit 10BitRegister
module _10BitRegister (
  input  [9:0] I,
  input  clk,
  input  W_Enable,
  output [9:0] Q
);

  RisingEdgeTriggeredDFlipFlop risingedgetriggereddflipflop_1 (.D(I[9]), .C(clk), .Q(Q[9]), .E(W_Enable));
  RisingEdgeTriggeredDFlipFlop risingedgetriggereddflipflop_2 (.D(I[8]), .C(clk), .Q(Q[8]), .E(W_Enable));
  RisingEdgeTriggeredDFlipFlop risingedgetriggereddflipflop_3 (.D(I[7]), .C(clk), .Q(Q[7]), .E(W_Enable));
  RisingEdgeTriggeredDFlipFlop risingedgetriggereddflipflop_4 (.D(I[6]), .C(clk), .Q(Q[6]), .E(W_Enable));
  RisingEdgeTriggeredDFlipFlop risingedgetriggereddflipflop_5 (.D(I[5]), .C(clk), .Q(Q[5]), .E(W_Enable));
  RisingEdgeTriggeredDFlipFlop risingedgetriggereddflipflop_6 (.D(I[4]), .C(clk), .Q(Q[4]), .E(W_Enable));
  RisingEdgeTriggeredDFlipFlop risingedgetriggereddflipflop_7 (.D(I[3]), .C(clk), .Q(Q[3]), .E(W_Enable));
  RisingEdgeTriggeredDFlipFlop risingedgetriggereddflipflop_8 (.D(I[2]), .C(clk), .Q(Q[2]), .E(W_Enable));
  RisingEdgeTriggeredDFlipFlop risingedgetriggereddflipflop_9 (.D(I[1]), .C(clk), .Q(Q[1]), .E(W_Enable));
  RisingEdgeTriggeredDFlipFlop risingedgetriggereddflipflop_10 (.D(I[0]), .C(clk), .Q(Q[0]), .E(W_Enable));

  // Notes on the sheet:
  //   clk: pull=down
  //   W_Enable: pull=down
  //   Q: pull=down
  //   I: pull=down
endmodule
