// Logisim project 20BitRegister.circ as structural Verilog: 1 circuit, main circuit 20BitRegister
module _20BitRegister (
  input  [19:0] I,
  input  clk,
  input  W_Enable,
  output [19:0] Q
);

  RisingEdgeTriggeredDFlipFlop risingedgetriggereddflipflop_1 (.D(I[19]), .C(clk), .Q(Q[19]), .E(W_Enable));
  RisingEdgeTriggeredDFlipFlop risingedgetriggereddflipflop_2 (.D(I[18]), .C(clk), .Q(Q[18]), .E(W_Enable));
  RisingEdgeTriggeredDFlipFlop risingedgetriggereddflipflop_3 (.D(I[17]), .C(clk), .Q(Q[17]), .E(W_Enable));
  RisingEdgeTriggeredDFlipFlop risingedgetriggereddflipflop_4 (.D(I[16]), .C(clk), .Q(Q[16]), .E(W_Enable));
  RisingEdgeTriggeredDFlipFlop risingedgetriggereddflipflop_5 (.D(I[15]), .C(clk), .Q(Q[15]), .E(W_Enable));
  RisingEdgeTriggeredDFlipFlop risingedgetriggereddflipflop_6 (.D(I[14]), .C(clk), .Q(Q[14]), .E(W_Enable));
  RisingEdgeTriggeredDFlipFlop risingedgetriggereddflipflop_7 (.D(I[13]), .C(clk), .Q(Q[13]), .E(W_Enable));
  RisingEdgeTriggeredDFlipFlop risingedgetriggereddflipflop_8 (.D(I[12]), .C(clk), .Q(Q[12]), .E(W_Enable));
  RisingEdgeTriggeredDFlipFlop risingedgetriggereddflipflop_9 (.D(I[11]), .C(clk), .Q(Q[11]), .E(W_Enable));
  RisingEdgeTriggeredDFlipFlop risingedgetriggereddflipflop_10 (.D(I[10]), .C(clk), .Q(Q[10]), .E(W_Enable));
  RisingEdgeTriggeredDFlipFlop risingedgetriggereddflipflop_11 (.D(I[9]), .C(clk), .Q(Q[9]), .E(W_Enable));
  RisingEdgeTriggeredDFlipFlop risingedgetriggereddflipflop_12 (.D(I[8]), .C(clk), .Q(Q[8]), .E(W_Enable));
  RisingEdgeTriggeredDFlipFlop risingedgetriggereddflipflop_13 (.D(I[7]), .C(clk), .Q(Q[7]), .E(W_Enable));
  RisingEdgeTriggeredDFlipFlop risingedgetriggereddflipflop_14 (.D(I[6]), .C(clk), .Q(Q[6]), .E(W_Enable));
  RisingEdgeTriggeredDFlipFlop risingedgetriggereddflipflop_15 (.D(I[5]), .C(clk), .Q(Q[5]), .E(W_Enable));
  RisingEdgeTriggeredDFlipFlop risingedgetriggereddflipflop_16 (.D(I[4]), .C(clk), .Q(Q[4]), .E(W_Enable));
  RisingEdgeTriggeredDFlipFlop risingedgetriggereddflipflop_17 (.D(I[3]), .C(clk), .Q(Q[3]), .E(W_Enable));
  RisingEdgeTriggeredDFlipFlop risingedgetriggereddflipflop_18 (.D(I[2]), .C(clk), .Q(Q[2]), .E(W_Enable));
  RisingEdgeTriggeredDFlipFlop risingedgetriggereddflipflop_19 (.D(I[1]), .C(clk), .Q(Q[1]), .E(W_Enable));
  RisingEdgeTriggeredDFlipFlop risingedgetriggereddflipflop_20 (.D(I[0]), .C(clk), .Q(Q[0]), .E(W_Enable));

  // Notes on the sheet:
  //   clk: pull=down
  //   Q: pull=down
  //   I: pull=down
  //   W_Enable: pull=down
endmodule
