// Logisim project 3BitRegister.circ as structural Verilog: 1 circuit, main circuit 3BitRegister
module _3BitRegister (
  input  [2:0] I,
  input  clk,
  input  W_Enable,
  output [2:0] Q
);

  RisingEdgeTriggeredDFlipFlop risingedgetriggereddflipflop_1 (.D(I[2]), .C(clk), .Q(Q[2]), .E(W_Enable));
  RisingEdgeTriggeredDFlipFlop risingedgetriggereddflipflop_2 (.D(I[1]), .C(clk), .Q(Q[1]), .E(W_Enable));
  RisingEdgeTriggeredDFlipFlop risingedgetriggereddflipflop_3 (.D(I[0]), .C(clk), .Q(Q[0]), .E(W_Enable));

  // Notes on the sheet:
  //   Q: pull=down
  //   clk: pull=down
  //   I: pull=down
  //   W_Enable: pull=down
endmodule
