// Logisim project RegisterFile.circ as structural Verilog: 1 circuit, main circuit RegisterFile
module RegisterFile (
  input  [3:0] W_Select,
  input  [19:0] W,
  input  clk,
  input  W_Enabled,
  input  [3:0] R_Select,
  output [19:0] R
);

  wire and_1_out, and_2_out, and_3_out, and_4_out, and_5_out, and_6_out, and_7_out, and_8_out, and_9_out,
       and_10_out, and_11_out, and_12_out, and_13_out, and_14_out, and_15_out, and_16_out, decoder_1_out0,
       decoder_1_out1, decoder_1_out2, decoder_1_out3, decoder_1_out4, decoder_1_out5, decoder_1_out6,
       decoder_1_out7, decoder_1_out8, decoder_1_out9, decoder_1_out10, decoder_1_out11, decoder_1_out12,
       decoder_1_out13, decoder_1_out14, decoder_1_out15;
  wire [19:0] n20bitregister_1_q, n20bitregister_2_q, n20bitregister_3_q, n20bitregister_4_q,
       n20bitregister_5_q, n20bitregister_6_q, n20bitregister_7_q, n20bitregister_8_q, n20bitregister_9_q,
       n20bitregister_10_q, n20bitregister_11_q, n20bitregister_12_q, n20bitregister_13_q,
       n20bitregister_14_q, n20bitregister_15_q, n20bitregister_16_q;

  and and_1 (and_1_out, decoder_1_out0, clk);
  and and_2 (and_2_out, decoder_1_out1, clk);
  _20BitRegister u_20bitregister_1 (.C(and_1_out), .I(W), .Q(n20bitregister_1_q), .E(W_Enabled));
  _20BitRegister u_20bitregister_2 (.C(and_2_out), .I(W), .Q(n20bitregister_2_q), .E(W_Enabled));
  and and_3 (and_3_out, decoder_1_out2, clk);
  and and_4 (and_4_out, decoder_1_out3, clk);
  _20BitRegister u_20bitregister_3 (.C(and_3_out), .I(W), .Q(n20bitregister_3_q), .E(W_Enabled));
  _20BitRegister u_20bitregister_4 (.C(and_4_out), .I(W), .Q(n20bitregister_4_q), .E(W_Enabled));
  and and_5 (and_5_out, decoder_1_out4, clk);
  and and_6 (and_6_out, decoder_1_out5, clk);
  _20BitRegister u_20bitregister_5 (.C(and_5_out), .I(W), .Q(n20bitregister_5_q), .E(W_Enabled));
  _20BitRegister u_20bitregister_6 (.C(and_6_out), .I(W), .Q(n20bitregister_6_q), .E(W_Enabled));
  and and_7 (and_7_out, decoder_1_out6, clk);
  and and_8 (and_8_out, decoder_1_out7, clk);
  _20BitRegister u_20bitregister_7 (.C(and_7_out), .I(W), .Q(n20bitregister_7_q), .E(W_Enabled));
  Decoder #(.select(4), .disabled(0), .enable("false")) decoder_1 (
    .out0(decoder_1_out0), .out1(decoder_1_out1), .out2(decoder_1_out2), .out3(decoder_1_out3),
    .out4(decoder_1_out4), .out5(decoder_1_out5), .out6(decoder_1_out6), .out7(decoder_1_out7),
    .out8(decoder_1_out8), .out9(decoder_1_out9), .out10(decoder_1_out10), .out11(decoder_1_out11),
    .out12(decoder_1_out12), .out13(decoder_1_out13), .out14(decoder_1_out14), .out15(decoder_1_out15),
    .sel(W_Select));
  _20BitRegister u_20bitregister_8 (.C(and_8_out), .I(W), .Q(n20bitregister_8_q), .E(W_Enabled));
  and and_9 (and_9_out, decoder_1_out8, clk);
  Multiplexer #(.select(4), .width(20), .disabled(0), .enable("false")) multiplexer_1 (
    .in0(n20bitregister_1_q), .in1(n20bitregister_2_q), .in2(n20bitregister_3_q), .in3(n20bitregister_4_q),
    .in4(n20bitregister_5_q), .in5(n20bitregister_6_q), .in6(n20bitregister_7_q), .in7(n20bitregister_8_q),
    .in8(n20bitregister_9_q), .in9(n20bitregister_10_q), .in10(n20bitregister_11_q),
    .in11(n20bitregister_12_q), .in12(n20bitregister_13_q), .in13(n20bitregister_14_q),
    .in14(n20bitregister_15_q), .in15(n20bitregister_16_q), .out(R), .sel(R_Select));
  and and_10 (and_10_out, decoder_1_out9, clk);
  _20BitRegister u_20bitregister_9 (.C(and_9_out), .I(W), .Q(n20bitregister_9_q), .E(W_Enabled));
  _20BitRegister u_20bitregister_10 (.C(and_10_out), .I(W), .Q(n20bitregister_10_q), .E(W_Enabled));
  and and_11 (and_11_out, decoder_1_out10, clk);
  and and_12 (and_12_out, decoder_1_out11, clk);
  _20BitRegister u_20bitregister_11 (.C(and_11_out), .I(W), .Q(n20bitregister_11_q), .E(W_Enabled));
  _20BitRegister u_20bitregister_12 (.C(and_12_out), .I(W), .Q(n20bitregister_12_q), .E(W_Enabled));
  and and_13 (and_13_out, decoder_1_out12, clk);
  and and_14 (and_14_out, decoder_1_out13, clk);
  _20BitRegister u_20bitregister_13 (.C(and_13_out), .I(W), .Q(n20bitregister_13_q), .E(W_Enabled));
  _20BitRegister u_20bitregister_14 (.C(and_14_out), .I(W), .Q(n20bitregister_14_q), .E(W_Enabled));
  and and_15 (and_15_out, decoder_1_out14, clk);
  and and_16 (and_16_out, decoder_1_out15, clk);
  _20BitRegister u_20bitregister_15 (.C(and_15_out), .I(W), .Q(n20bitregister_15_q), .E(W_Enabled));
  _20BitRegister u_20bitregister_16 (.C(and_16_out), .I(W), .Q(n20bitregister_16_q), .E(W_Enabled));

  // Notes on the sheet:
  //   W_Select: pull=down
  //   R_Select: pull=down
  //   W: pull=down
  //   R: pull=down
  //   clk: pull=down
  //   W_Enabled: pull=down
endmodule
